// Logisim project bcd.circ as structural Verilog: 1 circuit, main circuit implementation
module implementation (
  input  w3,
  input  w2,
  input  w1,
  input  w0,
  output a,
  output b,
  output c,
  output d,
  output e,
  output f,
  output g
);

  wire w0n, w0nw1_out, w0nw1n_out, w0nw2_out, w0nw2n_out, w0w1_out, w0w1n_out, w0w1nw2_out, w0w2_out, w1n,
       w1nw2_out, w1w2n_out, w2n, w2nw3_out, w3n;

  not not_1 (w3n, w3);
  not not_2 (w2n, w2);
  not not_3 (w1n, w1);
  not not_4 (w0n, w0);
  and w0w2 (w0w2_out, w0, w2);
  and w0nw2n (w0nw2n_out, w0n, w2n);
  and w2nw3 (w2nw3_out, w2n, w3);
  and w0w1 (w0w1_out, w0, w1);
  and w0nw1n (w0nw1n_out, w0n, w1n);
  and w0w1n (w0w1n_out, w1n, w0);
  and w0nw1 (w0nw1_out, w0n, w1);
  and w1w2n (w1w2n_out, w1, w2n);
  and w0nw2 (w0nw2_out, w0n, w2);
  and w1nw2 (w1nw2_out, w1n, w2);
  and w0w1nw2 (w0w1nw2_out, w0w1n_out, w2);
  or or_1 (a, w0w2_out, w0nw2n_out, w1, w2nw3_out);
  or or_2 (b, w0w1_out, w2n, w0nw1n_out);
  or or_3 (c, w0w1n_out, w0nw1n_out, w0w1_out, w2);
  or or_4 (d, w0w1nw2_out, w3, w0nw2n_out, w0nw1_out, w1w2n_out);
  or or_5 (e, w0nw1_out, w0nw2n_out);
  or or_6 (f, w0nw1n_out, w0nw2_out, w2nw3_out, w1nw2_out);
  or or_7 (g, w3, w1w2n_out, w1nw2_out, w0nw1_out);

  // Other names for the same wires on the sheet: at = a; bt = b; ct = c; dt = d; et = e; ft = f; gt = g; w0t = w0;
  //   w1t = w1; w2t = w2; w3t = w3
endmodule
